# Fritzing sketch circuit (saved by Fritzing 0.9.3b)
breadboards: 1

parts:
  Part1 = Arduino Uno (Rev3)
  VCC1 = 4 x AAA Battery Mount
  Part2 = Adafruit DRV8833 DC/Stepper Motor Driver [part_number="Adafruit #3297"]  # not connected
  J1 = Basic Servo
  M1 = DC Motor  # not connected
  M2 = DC Motor  # not connected

nets:
  N1: Part1.D8, J1.pulse
  GND: Part1.GND, VCC1.-, J1.gnd
  VIN: Part1.VIN, VCC1.+, J1.vcc

custom parts:
  Adafruit DRV8833 DC/Stepper Motor Driver: Spin two DC motors or step one bi-polar or uni-polar stepper with up to 1.2A per channel using the DRV8833. This motor driver chip is a nice alternative to the TB6612 driver. Like that chip, you get 2 full H-bridges, but this chip is better for low voltage uses (can run from 2.7V up to 10.8V motor power) and has built in current limiting capability. We set it up for 1A current limiting so you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
